# Fritzing sketch Schema stepper (saved by Fritzing 0.9.0b)
circuit board: 8.46667cm x 5.64444cm
breadboards: 1

parts:
  Composant1 = Arduino Uno (Rev3)
  M1 = Stepper Motor - Unipolar
  Power_plug1 = Power plug
  IC1 = ULN2003A [package="SO16 [SMD]"]
  IC2 = Voltage Regulator [package=78xxl]
  C1 = Electrolytic Capacitor [capacitance=10µF voltage=16V package="100 mil [THT, electrolytic]"]

nets:
  GND: Composant1.GND, Power_plug1.GND, IC1.0V, IC2.GND, C1.-
  N1: Composant1.D2, IC1.In_1
  N2: Composant1.D3_PWM, IC1.In_3
  N3: Composant1.D4, IC1.In_4
  N4: Composant1.D5_PWM, IC1.In_6
  N5: Composant1.VIN, IC2.IN, C1.+
  N6: M1.A, IC1.Out_1
  N7: M1.COMMON_1, M1.COMMON_2, Power_plug1.VCC, IC1.COM_-_Common, IC1.Out_5, IC1.Out_2, IC2.OUT
  N8: M1.C, IC1.Out_3
  N9: M1.B, IC1.Out_4
  N10: M1.D, IC1.Out_6

notes:
  5V (fonctionne aussi avec 9V)
  ULN3004A ou ULN2004A
